// Logisim project sap 1.circ as structural Verilog: 8 circuits, main circuit main
module main (
  input  OE,
  input  [7:0] Testing_Data,
  input  [3:0] OE_Testinf_Data,
  input  OE_Testing_Data,
  output [3:0] MAR_Content,
  output [3:0] Counter_Content,
  output [7:0] IR_content,
  output [7:0] MBR_Content,
  output [7:0] Regr_A_Content,
  output [7:0] ALU_Result,
  output [7:0] out_11,
  output [2:0] Counter_Content_2,
  output [7:0] Reg_B_Content
);

  wire Clock_out, cu_1_1_c0, cu_1_1_c1, cu_1_1_c2, cu_1_1_c3, cu_1_1_c4, cu_1_1_c5, cu_1_1_c6, cu_1_1_c7,
       cu_1_1_c8, cu_1_1_c9, cu_1_1_c10, cu_1_1_c11, cu_ii_1_c12, cu_ii_1_c13, cu_ii_1_c14, cu_ii_1_c15,
       undriven_2;
  wire [2:0] undriven;
  wire [3:0] bitselector_2_out, controlled_buffer_1_out, mar_1_dout;
  wire [7:0] alu_1_dout, bit_extender_1_out, bit_extender_2_out, register_1_dout;
  wire [31:0] decimal_decoder_1_dout, Decimal_Decoder_2_dout, decimal_decoder_3_dout, decimal_decoder_4_dout,
       decimal_decoder_5_dout;

  Clock Clock (.out(Clock_out));
  Counter #(.max('h3), .width(4)) counter (
    .D(controlled_buffer_1_out), .count(cu_1_1_c1), .Q(Counter_Content), .up(cu_1_1_c0), .clk(Clock_out));  // open: load, carry, clr
  Register register_1 (
    .Clock(Clock_out), .WE(cu_1_1_c7), .Din(alu_1_dout), .OE(cu_1_1_c8), .Dout(register_1_dout),
    .Stored_Data(IR_content));
  Decimal_Decoder decimal_decoder_1 (.Din(Regr_A_Content), .Dout(decimal_decoder_1_dout));
  Register register_2 (
    .Clock(Clock_out), .WE(cu_ii_1_c12), .Din(alu_1_dout), .Stored_Data(Regr_A_Content));  // open: OE, Dout
  ALU alu_1 (
    .Reg_A(Regr_A_Content), .Reg_B(Reg_B_Content), .OE(cu_1_1_c11), .Dout(alu_1_dout), .ALU_Result(ALU_Result));  // open: Carry_Out
  Register register_3 (
    .Clock(Clock_out), .WE(cu_ii_1_c13), .Din(alu_1_dout), .Stored_Data(Reg_B_Content));  // open: OE, Dout
  assign controlled_buffer_1_out = cu_1_1_c0 ? Counter_Content : 4'bz;  // Controlled_Buffer controlled_buffer_1
  assign bit_extender_1_out = {{4{Counter_Content[3]}}, Counter_Content};  // Bit_Extender bit_extender_1
  Decimal_Decoder Decimal_Decoder_2 (.Din(Reg_B_Content), .Dout(Decimal_Decoder_2_dout));
  Decimal_Decoder decimal_decoder_3 (.Din(bit_extender_1_out), .Dout(decimal_decoder_3_dout));
  _7_Segment_Display u_7_segment_display_1 (
    .g(decimal_decoder_1_dout[15]), .f(decimal_decoder_1_dout[14]), .a(decimal_decoder_1_dout[13]),
    .b(decimal_decoder_1_dout[12]), .e(decimal_decoder_1_dout[31]), .d(decimal_decoder_1_dout[30]),
    .c(decimal_decoder_1_dout[29]), .dp(decimal_decoder_1_dout[28]));
  _7_Segment_Display u_7_segment_display_2 (
    .g(decimal_decoder_1_dout[11]), .f(decimal_decoder_1_dout[10]), .a(decimal_decoder_1_dout[9]),
    .b(decimal_decoder_1_dout[8]), .e(decimal_decoder_1_dout[27]), .d(decimal_decoder_1_dout[26]),
    .c(decimal_decoder_1_dout[25]), .dp(decimal_decoder_1_dout[24]));
  _7_Segment_Display u_7_segment_display_3 (
    .g(Decimal_Decoder_2_dout[15]), .f(Decimal_Decoder_2_dout[14]), .a(Decimal_Decoder_2_dout[13]),
    .b(Decimal_Decoder_2_dout[12]), .e(Decimal_Decoder_2_dout[31]), .d(Decimal_Decoder_2_dout[30]),
    .c(Decimal_Decoder_2_dout[29]), .dp(Decimal_Decoder_2_dout[28]));
  _7_Segment_Display u_7_segment_display_4 (
    .g(Decimal_Decoder_2_dout[11]), .f(Decimal_Decoder_2_dout[10]), .a(Decimal_Decoder_2_dout[9]),
    .b(Decimal_Decoder_2_dout[8]), .e(Decimal_Decoder_2_dout[27]), .d(Decimal_Decoder_2_dout[26]),
    .c(Decimal_Decoder_2_dout[25]), .dp(Decimal_Decoder_2_dout[24]));
  _7_Segment_Display u_7_segment_display_5 (
    .g(decimal_decoder_3_dout[3]), .f(decimal_decoder_3_dout[2]), .a(decimal_decoder_3_dout[1]),
    .b(decimal_decoder_3_dout[0]), .e(decimal_decoder_3_dout[19]), .d(decimal_decoder_3_dout[18]),
    .c(decimal_decoder_3_dout[17]), .dp(decimal_decoder_3_dout[16]));
  _7_Segment_Display u_7_segment_display_6 (
    .g(decimal_decoder_1_dout[7]), .f(decimal_decoder_1_dout[6]), .a(decimal_decoder_1_dout[5]),
    .b(decimal_decoder_1_dout[4]), .e(decimal_decoder_1_dout[23]), .d(decimal_decoder_1_dout[22]),
    .c(decimal_decoder_1_dout[21]), .dp(decimal_decoder_1_dout[20]));
  _7_Segment_Display u_7_segment_display_7 (
    .g(decimal_decoder_1_dout[3]), .f(decimal_decoder_1_dout[2]), .a(decimal_decoder_1_dout[1]),
    .b(decimal_decoder_1_dout[0]), .e(decimal_decoder_1_dout[19]), .d(decimal_decoder_1_dout[18]),
    .c(decimal_decoder_1_dout[17]), .dp(decimal_decoder_1_dout[16]));
  _7_Segment_Display u_7_segment_display_8 (
    .g(Decimal_Decoder_2_dout[7]), .f(Decimal_Decoder_2_dout[6]), .a(Decimal_Decoder_2_dout[5]),
    .b(Decimal_Decoder_2_dout[4]), .e(Decimal_Decoder_2_dout[23]), .d(Decimal_Decoder_2_dout[22]),
    .c(Decimal_Decoder_2_dout[21]), .dp(Decimal_Decoder_2_dout[20]));
  _7_Segment_Display u_7_segment_display_9 (
    .g(Decimal_Decoder_2_dout[3]), .f(Decimal_Decoder_2_dout[2]), .a(Decimal_Decoder_2_dout[1]),
    .b(Decimal_Decoder_2_dout[0]), .e(Decimal_Decoder_2_dout[19]), .d(Decimal_Decoder_2_dout[18]),
    .c(Decimal_Decoder_2_dout[17]), .dp(Decimal_Decoder_2_dout[16]));
  BitSelector #(.group(4)) bitselector_1 (.in(register_1_dout), .out(controlled_buffer_1_out), .sel(1'b0));
  LED D7 (.in(alu_1_dout[7]));
  LED D6 (.in(alu_1_dout[6]));
  LED D5 (.in(alu_1_dout[5]));
  LED D4 (.in(alu_1_dout[4]));
  assign alu_1_dout = OE_Testing_Data ? Testing_Data : 8'bz;  // Controlled_Buffer controlled_buffer_2
  LED D2 (.in(alu_1_dout[2]));
  LED D1 (.in(alu_1_dout[1]));
  LED D3 (.in(alu_1_dout[3]));
  LED D0 (.in(alu_1_dout[0]));
  MAR mar_1 (
    .Clock(Clock_out), .WE(cu_1_1_c9), .Din(controlled_buffer_1_out), .OE(cu_1_1_c10), .Dout(mar_1_dout),
    .Stored_Data(MAR_Content));
  assign alu_1_dout = cu_1_1_c5 ? MBR_Content : 8'bz;  // Controlled_Buffer controlled_buffer_3
  Register register_4 (
    .Clock(Clock_out), .WE(cu_1_1_c4), .Din(alu_1_dout), .OE(cu_1_1_c6), .Dout(alu_1_dout),
    .Stored_Data(MBR_Content));
  Register register_5 (
    .Clock(Clock_out), .WE(cu_ii_1_c15), .Din(alu_1_dout), .OE(cu_ii_1_c14), .Dout(alu_1_dout),
    .Stored_Data(out_11));
  Decimal_Decoder decimal_decoder_4 (.Din(out_11), .Dout(decimal_decoder_4_dout));
  _7_Segment_Display u_7_segment_display_10 (
    .g(decimal_decoder_4_dout[15]), .f(decimal_decoder_4_dout[14]), .a(decimal_decoder_4_dout[13]),
    .b(decimal_decoder_4_dout[12]), .e(decimal_decoder_4_dout[31]), .d(decimal_decoder_4_dout[30]),
    .c(decimal_decoder_4_dout[29]), .dp(decimal_decoder_4_dout[28]));
  assign mar_1_dout = OE ? OE_Testinf_Data : 4'bz;  // Controlled_Buffer controlled_buffer_4
  _7_Segment_Display u_7_segment_display_11 (
    .g(decimal_decoder_4_dout[11]), .f(decimal_decoder_4_dout[10]), .a(decimal_decoder_4_dout[9]),
    .b(decimal_decoder_4_dout[8]), .e(decimal_decoder_4_dout[27]), .d(decimal_decoder_4_dout[26]),
    .c(decimal_decoder_4_dout[25]), .dp(decimal_decoder_4_dout[24]));
  _7_Segment_Display u_7_segment_display_12 (
    .g(decimal_decoder_4_dout[7]), .f(decimal_decoder_4_dout[6]), .a(decimal_decoder_4_dout[5]),
    .b(decimal_decoder_4_dout[4]), .e(decimal_decoder_4_dout[23]), .d(decimal_decoder_4_dout[22]),
    .c(decimal_decoder_4_dout[21]), .dp(decimal_decoder_4_dout[20]));
  _7_Segment_Display u_7_segment_display_13 (
    .g(decimal_decoder_4_dout[3]), .f(decimal_decoder_4_dout[2]), .a(decimal_decoder_4_dout[1]),
    .b(decimal_decoder_4_dout[0]), .e(decimal_decoder_4_dout[19]), .d(decimal_decoder_4_dout[18]),
    .c(decimal_decoder_4_dout[17]), .dp(decimal_decoder_4_dout[16]));
  LED D7_2 (.in(alu_1_dout[7]));
  LED D6_2 (.in(alu_1_dout[6]));
  LED D5_2 (.in(alu_1_dout[5]));
  LED D4_2 (.in(alu_1_dout[4]));
  LED D3_2 (.in(alu_1_dout[3]));
  LED D2_2 (.in(alu_1_dout[2]));
  LED D1_2 (.in(alu_1_dout[1]));
  LED D0_2 (.in(alu_1_dout[0]));
  // RAM #(.addrWidth(4)) ram_1: pin names not known; wires that end beside it: alu_1_dout[1], alu_1_dout[0]
  BitSelector #(.group(4)) bitselector_2 (.in(IR_content), .out(bitselector_2_out), .sel(1'b1));
  Counter #(.max('h5), .width(3)) counter_2 (
    .D(undriven), .count(undriven_2), .Q(Counter_Content_2), .clk(Clock_out));  // open: load, carry, clr
  CU_1 cu_1_1 (
    .OPC3(bitselector_2_out[3]), .OPC2(bitselector_2_out[2]), .OPC1(bitselector_2_out[1]),
    .OPC0(bitselector_2_out[0]), .SC2(Counter_Content_2[2]), .SC1(Counter_Content_2[1]),
    .SC0(Counter_Content_2[0]), .C0(cu_1_1_c0), .C1(cu_1_1_c1), .C2(cu_1_1_c2), .C3(cu_1_1_c3),
    .C4(cu_1_1_c4), .C5(cu_1_1_c5), .C6(cu_1_1_c6), .C7(cu_1_1_c7), .C8(cu_1_1_c8), .C9(cu_1_1_c9),
    .C10(cu_1_1_c10), .C11(cu_1_1_c11));
  CU_II cu_ii_1 (
    .OPC3(bitselector_2_out[3]), .OPC2(bitselector_2_out[2]), .OPC1(bitselector_2_out[1]),
    .OPC0(bitselector_2_out[0]), .SC2(Counter_Content_2[2]), .SC1(Counter_Content_2[1]),
    .SC0(Counter_Content_2[0]), .C12(cu_ii_1_c12), .C13(cu_ii_1_c13), .C14(cu_ii_1_c14), .C15(cu_ii_1_c15));
  assign bit_extender_2_out = {{5{Counter_Content_2[2]}}, Counter_Content_2};  // Bit_Extender bit_extender_2
  _7_Segment_Display u_7_segment_display_14 (
    .g(decimal_decoder_5_dout[3]), .f(decimal_decoder_5_dout[2]), .a(decimal_decoder_5_dout[1]),
    .b(decimal_decoder_5_dout[0]), .e(decimal_decoder_5_dout[19]), .d(decimal_decoder_5_dout[18]),
    .c(decimal_decoder_5_dout[17]), .dp(decimal_decoder_5_dout[16]));
  Decimal_Decoder decimal_decoder_5 (.Din(bit_extender_2_out), .Dout(decimal_decoder_5_dout));

  // Notes on the sheet:
  //   Program Counter
  //   Instruction Register
  //   Register A
  //   ALU
  //   Register B
  //   Internal Data Bus
  //   Output Register
  //   MAR
  //   MBR
  //   External Data Bus
  //   Step Counter
  //   C15
  //   C14
  //   C13
  //   CUI I
  //   CUI II
  //   C12
  //   C11
  //   C10
  //   C9
  //   C8
  //   C7
  //   C6
  //   C5
  //   C4
  //   C3
  //   C2
  //   C1
  //   C0
endmodule

module Register (
  input  Clock,
  input  WE,
  input  [7:0] Din,
  input  OE,
  output [7:0] Dout,
  output [7:0] Stored_Data
);

  Memory_cell _0 (
    .Clock(Clock), .WE(WE), .Din(Din[0]), .OE(OE), .Dout(Dout[0]), .Stored_Data(Stored_Data[0]));  // open: Reset
  Memory_cell _1 (
    .Clock(Clock), .WE(WE), .Din(Din[1]), .OE(OE), .Dout(Dout[1]), .Stored_Data(Stored_Data[1]));  // open: Reset
  Memory_cell _2 (
    .Clock(Clock), .WE(WE), .Din(Din[2]), .OE(OE), .Dout(Dout[2]), .Stored_Data(Stored_Data[2]));  // open: Reset
  Memory_cell _3 (
    .Clock(Clock), .WE(WE), .Din(Din[3]), .OE(OE), .Dout(Dout[3]), .Stored_Data(Stored_Data[3]));  // open: Reset
  Memory_cell _4 (
    .Clock(Clock), .WE(WE), .Din(Din[4]), .OE(OE), .Dout(Dout[4]), .Stored_Data(Stored_Data[4]));  // open: Reset
  Memory_cell _5 (
    .Clock(Clock), .WE(WE), .Din(Din[5]), .OE(OE), .Dout(Dout[5]), .Stored_Data(Stored_Data[5]));  // open: Reset
  Memory_cell _6 (
    .Clock(Clock), .WE(WE), .Din(Din[6]), .OE(OE), .Dout(Dout[6]), .Stored_Data(Stored_Data[6]));  // open: Reset
  Memory_cell _7 (
    .Clock(Clock), .WE(WE), .Din(Din[7]), .OE(OE), .Dout(Dout[7]), .Stored_Data(Stored_Data[7]));  // open: Reset

  // Notes on the sheet:
  //   Register ( 8 Bits )
endmodule

module Memory_cell (
  input  Clock,
  input  WE,
  input  Din,
  input  OE,
  input  Reset,
  output Dout,
  output Stored_Data
);

  wire and_1_out, and_2_out, not_1_out, or_1_out;

  not not_1 (not_1_out, WE);
  and and_1 (and_1_out, Stored_Data, not_1_out);
  and and_2 (and_2_out, WE, Din);
  or or_1 (or_1_out, and_1_out, and_2_out);
  D_Flip_Flop #(.enable("true")) d_ff_1 (
    .clk(Clock), .D(or_1_out), .Q(Stored_Data), .reset(Reset));  // open: Qn, preset, en
  assign Dout = OE ? Stored_Data : 1'bz;  // Controlled_Buffer controlled_buffer_1

  // Notes on the sheet:
  //   Memory Cell
endmodule

module MAR (
  input  Clock,
  input  WE,
  input  [3:0] Din,
  input  OE,
  output [3:0] Dout,
  output [3:0] Stored_Data
);

  Memory_cell _0 (
    .Clock(Clock), .WE(WE), .Din(Din[0]), .OE(OE), .Dout(Dout[0]), .Stored_Data(Stored_Data[0]));  // open: Reset
  Memory_cell _1 (
    .Clock(Clock), .WE(WE), .Din(Din[1]), .OE(OE), .Dout(Dout[1]), .Stored_Data(Stored_Data[1]));  // open: Reset
  Memory_cell _2 (
    .Clock(Clock), .WE(WE), .Din(Din[2]), .OE(OE), .Dout(Dout[2]), .Stored_Data(Stored_Data[2]));  // open: Reset
  Memory_cell _3 (
    .Clock(Clock), .WE(WE), .Din(Din[3]), .OE(OE), .Dout(Dout[3]), .Stored_Data(Stored_Data[3]));  // open: Reset

  // Notes on the sheet:
  //   MAR
endmodule

module ALU (
  input  [7:0] Reg_A,
  input  [7:0] Reg_B,
  input  OE,
  output [7:0] Dout,
  output [7:0] ALU_Result,
  output Carry_Out
);

  Adder adder_1 (.a(Reg_A), .b(Reg_B), .out(ALU_Result), .cout(Carry_Out));  // open: cin
  assign Dout = OE ? ALU_Result : 8'bz;  // Controlled_Buffer controlled_buffer_1

  // Notes on the sheet:
  //   ALU ( 8 Bits )
endmodule

module Decimal_Decoder (
  input  [7:0] Din,
  output [31:0] Dout
);

  ROM #(.dataWidth(32)) rom_1 (
    .addr(Din),
    .data({Dout[31:28], Dout[15:12], Dout[27:24], Dout[11:8], Dout[23:20], Dout[7:4], Dout[19:16], Dout[3:0]}));

  // Notes on the sheet:
  //   Decimal Decoder
  //   contents of rom_1 (hex, n*v repeats v):
  //   e7 21 cb 6b 2d 6e ee 23 ef 2f 21e7 2121 21cb 216b 212d 216e 21ee 2123 21ef 212f cbe7 cb21 cbcb cb6b
  //   cb2d cb6e cbee cb23 cbef cb2f 6be7 6b21 6bcb 6b6b 6b2d 6b6e 6bee 6b23 6bef 6b2f 2de7 2d21 2dcb 2d6b
  //   2d2d 2d6e 2dee 2d23 2def 2d2f 6ee7 6e21 6ecb 6e6b 6e2d 6e6e 6eee 6e23 6eef 6e2f eee7 ee21 eecb ee6b
  //   ee2d ee6e eeee ee23 eeef ee2f 23e7 2321 23cb 236b 232d 236e 23ee 2323 23ef 232f efe7 ef21 efcb ef6b
  //   ef2d ef6e efee ef23 efef ef2f 2fe7 2f21 2fcb 2f6b 2f2d 2f6e 2fee 2f23 2fef 2f2f 21e7e7 21e721 21e7cb
  //   21e76b 21e72d 21e76e 21e7ee 21e723 21e7ef 21e72f 2121e7 212121 2121cb 21216b 21212d 21216e 2121ee
  //   212123 2121ef 21212f 21cbe7 21cb21 21cbcb 21cb6b 21cb2d 21cb6e 21cbee 21cb23 21cbef 21cb2f 216be7
  //   216b21 216bcb 216b6b 216b2d 216b6e 216bee 216b23 216bef 216b2f 212de7 212d21 212dcb 212d6b 212d2d
  //   212d6e 212dee 212d23 212def 212d2f 216ee7 216e21 216ecb 216e6b 216e2d 216e6e 216eee 216e23 216eef
  //   216e2f 21eee7 21ee21 21eecb 21ee6b 21ee2d 21ee6e 21eeee 21ee23 21eeef 21ee2f 2123e7 212321 2123cb
  //   21236b 21232d 21236e 2123ee 212323 2123ef 21232f 21efe7 21ef21 21efcb 21ef6b 21ef2d 21ef6e 21efee
  //   21ef23 21efef 21ef2f 212fe7 212f21 212fcb 212f6b 212f2d 212f6e 212fee 212f23 212fef 212f2f cbe7e7
  //   cbe721 cbe7cb cbe76b cbe72d cbe76e cbe7ee cbe723 cbe7ef cbe72f cb21e7 cb2121 cb21cb cb216b cb212d
  //   cb216e cb21ee cb2123 cb21ef cb212f cbcbe7 cbcb21 cbcbcb cbcb6b cbcb2d cbcb6e cbcbee cbcb23 cbcbef
  //   cbcb2f cb6be7 cb6b21 cb6bcb cb6b6b cb6b2d cb6b6e cb6bee cb6b23 cb6bef cb6b2f cb2de7 cb2d21 cb2dcb
  //   cb2d6b cb2d2d cb2d6e cb2dee cb2d23 cb2def cb2d2f cb6ee7 cb6e21 cb6ecb cb6e6b cb6e2d cb6e6e
endmodule

module CU_1 (
  input  OPC3,
  input  OPC2,
  input  OPC1,
  input  OPC0,
  input  SC2,
  input  SC1,
  input  SC0,
  output C0,
  output C1,
  output C2,
  output C3,
  output C4,
  output C5,
  output C6,
  output C7,
  output C8,
  output C9,
  output C10,
  output C11
);

  wire and_4_out, and_5_out, and_6_out, and_7_out, and_8_out, and_9_out, and_10_out, and_13_out, and_14_out,
       and_15_out, and_16_out, and_17_out, and_18_out, and_19_out, and_20_out, not_1_out, not_2_out,
       not_3_out, not_4_out, not_5_out, not_6_out, not_7_out, not_8_out, not_9_out, not_10_out, not_11_out,
       not_12_out, not_13_out, not_14_out, not_15_out, not_16_out, not_17_out, not_18_out, not_19_out,
       not_20_out, not_21_out, not_22_out, not_23_out, not_24_out, not_25_out, not_26_out, not_27_out,
       not_28_out, not_29_out, not_30_out, not_31_out, not_32_out, not_33_out, not_34_out, not_35_out,
       not_36_out, not_37_out, not_38_out, not_39_out, not_40_out, not_41_out, not_42_out, not_43_out,
       not_44_out;

  not not_1 (not_1_out, SC2);
  not not_2 (not_2_out, SC1);
  not not_3 (not_3_out, SC0);
  not not_4 (not_4_out, SC2);
  not not_5 (not_5_out, SC1);
  not not_6 (not_6_out, SC1);
  not not_7 (not_7_out, SC0);
  not not_8 (not_8_out, SC2);
  not not_9 (not_9_out, SC1);
  not not_10 (not_10_out, OPC1);
  not not_11 (not_11_out, SC1);
  not not_12 (not_12_out, SC0);
  not not_13 (not_13_out, SC2);
  not not_14 (not_14_out, SC1);
  not not_15 (not_15_out, OPC1);
  not not_16 (not_16_out, SC1);
  not not_17 (not_17_out, SC0);
  not not_18 (not_18_out, SC2);
  not not_19 (not_19_out, SC2);
  not not_20 (not_20_out, SC0);
  not not_21 (not_21_out, OPC1);
  not not_22 (not_22_out, SC1);
  not not_23 (not_23_out, SC1);
  not not_24 (not_24_out, SC0);
  not not_25 (not_25_out, SC2);
  not not_26 (not_26_out, SC0);
  not not_27 (not_27_out, OPC1);
  not not_28 (not_28_out, SC2);
  not not_29 (not_29_out, SC2);
  not not_30 (not_30_out, SC2);
  not not_31 (not_31_out, SC1);
  not not_32 (not_32_out, SC0);
  not not_33 (not_33_out, OPC1);
  not not_34 (not_34_out, SC2);
  not not_35 (not_35_out, SC2);
  not not_36 (not_36_out, SC2);
  not not_37 (not_37_out, SC1);
  not not_38 (not_38_out, OPC1);
  not not_39 (not_39_out, SC1);
  not not_40 (not_40_out, SC0);
  not not_41 (not_41_out, SC1);
  not not_42 (not_42_out, SC0);
  not not_43 (not_43_out, OPC0);
  not not_44 (not_44_out, SC2);
  and and_1 (C0, not_1_out, not_2_out, not_3_out);
  and and_2 (C1, not_4_out, not_5_out, SC0);
  and and_3 (C2, OPC0, not_6_out);
  and and_4 (and_4_out, not_8_out, not_9_out, SC0);
  and and_5 (and_5_out, not_10_out, SC2, not_11_out, not_12_out);
  and and_6 (and_6_out, not_13_out, not_14_out, SC0);
  and and_7 (and_7_out, not_15_out, SC2, not_16_out, not_17_out);
  and and_8 (and_8_out, OPC1, OPC0, not_18_out, SC0);
  and and_9 (and_9_out, not_19_out, SC1, not_20_out);
  and and_10 (and_10_out, not_21_out, SC2, not_22_out, SC0);
  and and_11 (C6, OPC0, not_23_out);
  and and_12 (C7, not_25_out, SC1, not_26_out);
  and and_13 (and_13_out, not_27_out, not_28_out, SC1, SC0);
  and and_14 (and_14_out, OPC0, not_29_out, SC1, SC0);
  and and_15 (and_15_out, not_30_out, not_31_out, not_32_out);
  and and_16 (and_16_out, not_33_out, not_34_out, SC1, SC0);
  and and_17 (and_17_out, OPC0, not_35_out, SC1, SC0);
  and and_18 (and_18_out, not_36_out, not_37_out, SC0);
  and and_19 (and_19_out, not_38_out, SC2, not_39_out, not_40_out);
  and and_20 (and_20_out, OPC0, SC2, not_41_out, not_42_out);
  and and_21 (C11, not_43_out, SC1);
  or or_1 (C3, and_4_out, and_5_out);
  or or_2 (C4, and_6_out, and_7_out, and_8_out);
  or or_3 (C5, and_9_out, and_10_out);
  or or_4 (C8, and_13_out, and_14_out);
  or or_5 (C9, and_15_out, and_16_out, and_17_out);
  or or_6 (C10, and_18_out, and_19_out, and_20_out);
endmodule

module CU_II (
  input  OPC3,
  input  OPC2,
  input  OPC1,
  input  OPC0,
  input  SC2,
  input  SC1,
  input  SC0,
  output C12,
  output C13,
  output C14,
  output C15
);

  wire not_1_out, not_2_out, not_3_out, not_4_out, not_5_out, not_6_out, not_7_out, not_8_out;

  not not_1 (not_1_out, OPC1);
  not not_2 (not_2_out, OPC0);
  not not_3 (not_3_out, SC1);
  not not_4 (not_4_out, OPC1);
  not not_5 (not_5_out, SC1);
  not not_6 (not_6_out, SC2);
  not not_7 (not_7_out, OPC0);
  not not_8 (not_8_out, SC2);
  and and_1 (C12, not_2_out, not_3_out);
  and and_2 (C13, OPC0, not_5_out);
  and and_3 (C14, OPC0, SC1);
  and and_4 (C15, not_7_out, SC1);
endmodule
